// Logisim project cpu.circ as structural Verilog: 1 circuit, main circuit main
module main (
);

  wire A_WRITE, ALU_CARRY, ALU_MODE, ALU_S0, ALU_S1, ALU_S2, ALU_S3, and_1_out, and_2_out, and_3_out,
       and_4_out, B_WRITE, button_1_out, button_2_out, C_WRITE, CARRY, CLK, clock_1_out, d_ff_1_q, D_WRITE,
       E_WRITE, END_INSTR, EQUAL, FLAGS_SYS_UPDATE, FLAGS_USR_UPDATE, IE_qn, IE_TOGGLE, INTERRUPT, IR_WRITE,
       l_74181_700a1432_1_p16, l_74181_700a1432_2_p2, l_74181_700a1432_2_p20, nA_OUT, nAH_OUT, nAL_OUT,
       nALU_OUT, nBC_OUT, nDE_OUT, not_1_out, not_2_out, not_3_out, not_4_out, not_5_out, not_6_out,
       not_7_out, not_8_out, not_9_out, not_10_out, not_11_out, nPC_OUT, nRAM_OUT, nRAM_WRITE, nSP_OUT,
       nT_OUT, PC_H_WRITE, PC_L_WRITE, RST, SP_H_WRITE, SP_L_WRITE, T_WRITE;
  wire [3:0] STEP_q;
  wire [6:0] keyboard_1_data;
  wire [7:0] ACC_q, B_q, C_q, controlled_buffer_5_out, D_q, E_q, IR_q, l_74181_700a1432_2_p22, PC_H_q,
       PC_L_q, ram_1_data, register_1_q, register_2_q, SP_H_q, SP_L_q, TMP_q;
  wire [7:4] d_ff_2_q;
  wire [15:0] controlled_buffer_1_out;
  wire [31:8] rom_1_data;

  // Probe on l_74181_700a1432_2_p22
  Register PC_H (.D(l_74181_700a1432_2_p22), .en(1'b1), .clk(PC_H_WRITE), .Q(PC_H_q));  // open: clr
  Register PC_L (.D(l_74181_700a1432_2_p22), .en(1'b1), .clk(PC_L_WRITE), .Q(PC_L_q));  // open: clr
  Register SP_H (.D(l_74181_700a1432_2_p22), .en(1'b1), .clk(SP_H_WRITE), .Q(SP_H_q), .clr(RST));
  Register SP_L (.D(l_74181_700a1432_2_p22), .en(1'b1), .clk(SP_L_WRITE), .Q(SP_L_q), .clr(RST));
  Register B (.D(l_74181_700a1432_2_p22), .en(1'b1), .clk(B_WRITE), .Q(B_q), .clr(RST));
  Register C (.D(l_74181_700a1432_2_p22), .en(1'b1), .clk(C_WRITE), .Q(C_q), .clr(RST));
  Register D (.D(l_74181_700a1432_2_p22), .en(1'b1), .clk(D_WRITE), .Q(D_q), .clr(RST));
  Register E (.D(l_74181_700a1432_2_p22), .en(1'b1), .clk(E_WRITE), .Q(E_q), .clr(RST));
  assign controlled_buffer_1_out = not_1_out ? {PC_H_q, PC_L_q} : 16'bz;  // Controlled_Buffer controlled_buffer_1
  not not_1 (not_1_out, nPC_OUT);
  assign controlled_buffer_1_out = not_2_out ? {SP_H_q, SP_L_q} : 16'bz;  // Controlled_Buffer controlled_buffer_2
  not not_2 (not_2_out, nSP_OUT);
  assign controlled_buffer_1_out = not_3_out ? {B_q, C_q} : 16'bz;  // Controlled_Buffer controlled_buffer_3
  not not_3 (not_3_out, nBC_OUT);
  assign controlled_buffer_1_out = not_4_out ? {D_q, E_q} : 16'bz;  // Controlled_Buffer controlled_buffer_4
  not not_4 (not_4_out, nDE_OUT);
  // Probe on controlled_buffer_1_out
  Pull_Resistor pull_resistor_1 (.node(controlled_buffer_1_out));
  not not_5 (not_5_out, nAH_OUT);
  assign controlled_buffer_5_out = not_5_out ? controlled_buffer_1_out[15:8] : 8'bz;  // Controlled_Buffer controlled_buffer_5
  assign controlled_buffer_5_out = not_6_out ? controlled_buffer_1_out[7:0] : 8'bz;  // Controlled_Buffer controlled_buffer_6
  not not_6 (not_6_out, nAL_OUT);
  Button button_1 (.out(button_1_out));
  Button button_2 (.out(button_2_out));
  RAM #(.addrWidth(15), .asyncread("true"), .databus("bidir"), .\type ("nonvolatile")) ram_1 (
    .addr(controlled_buffer_1_out[14:0]), .we(and_1_out), .oe(and_2_out), .clk(CLK), .data(ram_1_data));
  and and_1 (and_1_out, ~controlled_buffer_1_out[15], ~nRAM_WRITE);  // AND_Gate
  and and_2 (and_2_out, ~controlled_buffer_1_out[15], ~nRAM_OUT);  // AND_Gate
  TTY tty_1 (.data(ram_1_data[6:0]), .clk(CLK), .we(and_3_out), .clr(RST));
  and and_3 (and_3_out, controlled_buffer_1_out[15], ~nRAM_WRITE);  // AND_Gate
  and and_4 (and_4_out, controlled_buffer_1_out[15], ~nRAM_OUT);  // AND_Gate
  D_Flip_Flop d_ff_1 (.D(1'b0), .Q(d_ff_1_q), .preset(button_1_out), .reset(button_2_out));  // open: clk, Qn
  Keyboard keyboard_1 (.clk(CLK), .re(and_4_out), .clr(RST), .avail(INTERRUPT), .data(keyboard_1_data));
  Clock clock_1 (.out(clock_1_out));
  Button button_3 (.out(RST));
  and and_5 (CLK, d_ff_1_q, clock_1_out);
  assign ram_1_data = and_4_out ? {1'b0, keyboard_1_data} : 8'bz;  // Controlled_Buffer controlled_buffer_7
  not not_7 (not_7_out, nALU_OUT);
  assign ram_1_data = not_7_out ? l_74181_700a1432_2_p22 : 8'bz;  // Controlled_Buffer controlled_buffer_8
  // Probe on ram_1_data
  Pull_Resistor pull_resistor_2 (.node(ram_1_data));
  // Probe on l_74181_700a1432_2_p22
  D_Flip_Flop d_ff_2 (.D(CARRY), .clk(FLAGS_USR_UPDATE), .Q(d_ff_2_q[4]));  // open: Qn, preset, reset
  D_Flip_Flop d_ff_3 (.D(EQUAL), .clk(FLAGS_USR_UPDATE), .Q(d_ff_2_q[5]));  // open: Qn, preset, reset
  D_Flip_Flop d_ff_4 (.D(CARRY), .clk(FLAGS_SYS_UPDATE), .Q(d_ff_2_q[6]));  // open: Qn, preset, reset
  D_Flip_Flop d_ff_5 (.D(INTERRUPT), .clk(END_INSTR), .Q(d_ff_2_q[7]), .reset(IE_qn));  // open: Qn, preset
  D_Flip_Flop IE (.D(IE_qn), .clk(IE_TOGGLE), .Qn(IE_qn), .reset(RST));  // open: Q, preset
  Register IR (.D(ram_1_data), .clk(IR_WRITE), .Q(IR_q), .clr(RST));  // open: en
  Register ACC (.D(l_74181_700a1432_2_p22), .clk(A_WRITE), .Q(ACC_q), .clr(RST));  // open: en
  Register TMP (.D(l_74181_700a1432_2_p22), .clk(T_WRITE), .Q(TMP_q), .clr(RST));  // open: en
  Counter #(.max('hf), .width(4)) STEP (
    .load(RST), .D(4'b0000), .count(1'b1), .Q(STEP_q), .clk(CLK), .clr(END_INSTR));  // open: carry, up
  Register #(.trigger("high")) register_1 (.D({d_ff_2_q, STEP_q}), .clk(CLK), .Q(register_1_q));  // open: en, clr
  Register #(.trigger("high")) register_2 (.D(IR_q), .clk(CLK), .Q(register_2_q));  // open: en, clr
  assign controlled_buffer_5_out = not_8_out ? ACC_q : 8'bz;  // Controlled_Buffer controlled_buffer_9
  not not_8 (not_8_out, nA_OUT);
  Pull_Resistor pull_resistor_3 (.node(controlled_buffer_5_out));
  assign ram_1_data = not_9_out ? TMP_q : 8'bz;  // Controlled_Buffer controlled_buffer_10
  not not_9 (not_9_out, nT_OUT);
  // Probe on controlled_buffer_5_out
  // Probe on ram_1_data
  ROM #(.addrWidth(16), .dataWidth(32)) rom_1 (
    .addr({register_2_q, register_1_q}),
    .data({rom_1_data[31:24], ALU_S3, ALU_S2, ALU_S1, ALU_S0, ALU_CARRY, nAL_OUT, ALU_MODE, nAH_OUT, rom_1_data[15:8], nRAM_OUT, nDE_OUT, nBC_OUT, nT_OUT, nA_OUT, nPC_OUT, nALU_OUT, nSP_OUT}));
  // L_74181_700a1432 l_74181_700a1432_1: pin names not known; wires that end beside it: ALU_S3, ALU_S2, ALU_S1, ALU_S0, ram_1_data[7], controlled_buffer_5_out[7], ram_1_data[6], controlled_buffer_5_out[6], ram_1_data[5], controlled_buffer_5_out[5], ram_1_data[4], controlled_buffer_5_out[4], CARRY, l_74181_700a1432_2_p22[7], l_74181_700a1432_2_p22[6], l_74181_700a1432_1_p16, l_74181_700a1432_2_p22[5], l_74181_700a1432_2_p22[4]
  // L_74181_700a1432 l_74181_700a1432_2: pin names not known; wires that end beside it: ALU_MODE, l_74181_700a1432_2_p2, ALU_S3, ALU_S2, ALU_S1, ALU_S0, ram_1_data[3], controlled_buffer_5_out[3], ram_1_data[2], controlled_buffer_5_out[2], ram_1_data[1], controlled_buffer_5_out[1], ram_1_data[0], controlled_buffer_5_out[0], ALU_MODE, ALU_CARRY, l_74181_700a1432_2_p2, l_74181_700a1432_2_p22[3], l_74181_700a1432_2_p22[2], l_74181_700a1432_2_p20, l_74181_700a1432_2_p22[1], l_74181_700a1432_2_p22[0]
  and and_6 (EQUAL, l_74181_700a1432_1_p16, l_74181_700a1432_2_p20);
  not not_10 (not_10_out, CLK);
  not not_11 (not_11_out, CLK);
  assign {D_WRITE, E_WRITE, SP_L_WRITE, C_WRITE, PC_L_WRITE, B_WRITE, SP_H_WRITE, PC_H_WRITE} = not_10_out ? rom_1_data[15:8] : 8'bz;  // Controlled_Buffer controlled_buffer_11
  Pull_Resistor pull_resistor_4 (.node(PC_H_WRITE));
  assign {FLAGS_SYS_UPDATE, FLAGS_USR_UPDATE, IR_WRITE, IE_TOGGLE, END_INSTR, nRAM_WRITE, T_WRITE, A_WRITE} = not_11_out ? rom_1_data[31:24] : 8'bz;  // Controlled_Buffer controlled_buffer_12
  Pull_Resistor pull_resistor_5 (.node(A_WRITE));
  Pull_Resistor pull_resistor_6 (.node(SP_H_WRITE));
  Pull_Resistor pull_resistor_7 (.node(B_WRITE));
  Pull_Resistor pull_resistor_8 (.node(PC_L_WRITE));
  Pull_Resistor pull_resistor_9 (.node(C_WRITE));
  Pull_Resistor #(.pull(1)) pull_resistor_10 (.node(nRAM_WRITE));
  Pull_Resistor pull_resistor_11 (.node(T_WRITE));
  Pull_Resistor pull_resistor_12 (.node(END_INSTR));
  Pull_Resistor pull_resistor_13 (.node(IE_TOGGLE));
  Pull_Resistor pull_resistor_14 (.node(SP_L_WRITE));
  Pull_Resistor pull_resistor_15 (.node(E_WRITE));
  Pull_Resistor pull_resistor_16 (.node(D_WRITE));
  Pull_Resistor pull_resistor_17 (.node(IR_WRITE));
  Pull_Resistor pull_resistor_18 (.node(FLAGS_USR_UPDATE));
  Pull_Resistor pull_resistor_19 (.node(FLAGS_SYS_UPDATE));

  // Notes on the sheet:
  //   contents of rom_1 (hex, n*v repeats v):
  //   437087b 405017b 2405007b 13*c0500ff 437087b 405017b 2405007b 13*c0500ff 437087b 405017b 2405007b
  //   13*c0500ff 437087b 405017b 2405007b 13*c0500ff 437087b 405017b 2405007b 13*c0500ff 437087b 405017b
  //   2405007b 13*c0500ff 437087b 405017b 2405007b 13*c0500ff 437087b 405017b 2405007b 13*c0500ff 84f920fe
  //   40c02fe 60900fb 500ee 84f920fe 40c02fe 60c00fb 500ee 437087b 1c37017e 6*c0500ff 84f920fe 40c02fe
  //   60900fb 500ee 84f920fe 40c02fe 60c00fb 500ee 437087b 1c37017e 6*c0500ff 84f920fe 40c02fe 60900fb
  //   500ee 84f920fe 40c02fe 60c00fb 500ee 437087b 1c37017e 6*c0500ff 84f920fe 40c02fe 60900fb 500ee
  //   84f920fe 40c02fe 60c00fb 500ee 437087b 1c37017e 6*c0500ff 84f920fe 4fc02fe 60900fb 500ee 84f920fe
  //   4fc02fe 60c00fb 500ee 437087b 1c37017e 6*c0500ff 84f920fe 4fc02fe 60900fb 500ee 84f920fe 4fc02fe
  //   60c00fb 500ee 437087b 1c37017e 6*c0500ff 84f920fe 4fc02fe 60900fb 500ee 84f920fe 4fc02fe 60c00fb
  //   500ee 437087b 1c37017e 6*c0500ff 84f920fe 4fc02fe 60900fb 500ee 84f920fe 4fc02fe 60c00fb 500ee
  //   437087b 1c37017e 6*c0500ff a401087b 40401fb 5a7007b 840108fb c0401fb 11*c0500ff a401087b 40401fb
  //   5a7007b 840108fb c0401fb 11*c0500ff a401087b 40401fb 5a7007b 840108fb c0401fb 11*c0500ff a401087b
  //   40401fb 5a7007b 840108fb c0401fb 11*c0500ff a401087b 40c01fb 5a7007b 840108fb c0c01fb 11*c0500ff
  //   a401087b 40c01fb 5a7007b 840108fb c0c01fb 11*c0500ff a401087b 40c01fb 5a7007b 840108fb c0c01fb
  //   11*c0500ff a401087b 40c01fb 5a7007b 840108fb c0c01fb 11*c0500ff 84f920fe 40c02fe 60900fb 500ee
  //   84f920fe 40c02fe 60c00fb 500ee 437087b 1c37017e 6*c0500ff 84f920fe 40c02fe 60900fb 500ee 84f920fe
  //   40c02fe 60c00fb 500ee 437087b 1c37017e 6*c0500ff 84f920fe 40c02fe 60900fb 500ee 84f920fe 40c02fe
  //   60c00fb 500ee 437087b 1c37017e 6*c0500ff 84f920fe 40c02fe 60900fb 500ee 84f920fe 40c02fe 60c00fb
  //   500ee 437087b 1c37017e 6*c0500ff 84f920fe 4fc02fe 60900fb 500ee 84f920fe 4fc02fe 60c00fb 500ee
  //   437087b 1c37017e 6*c0500ff 84f920fe 4fc02fe 60900fb 500ee 84f920fe 4fc02fe 60c00fb 500ee 437087b
  //   1c37017e 6*c0500ff 84f920fe 4fc02fe 60900fb 500ee 84f920fe 4fc02fe 60c00fb 500ee 437087b 1c37017e
  //   6*c0500ff 84f920fe 4fc02fe 60900fb 500ee 84f920fe 4fc02fe 60c00fb 500ee 437087b 1c37017e 6*c0500ff
  //   a401087b 40401fb 4a7047b 840108fb c0401fb 11*c0500ff a401087b 40401fb 4a7047b 840108fb c0401fb
  //   11*c0500ff a401087b 40401fb 4a7047b 840108fb c0401fb 11*c0500ff a401087b 40401fb 4a7047b 840108fb
  //   c0401fb 11*c0500ff a401087b 40c01fb 4a7047b 840108fb c0c01fb 11*c0500ff a401087b 40c01fb 4a7047b
  //   840108fb c0c01fb 11*c0500ff a401087b 40c01fb 4a7047b 840108fb c0c01fb 11*c0500ff a401087b 40c01fb
  //   4a7047b 840108fb c0c01fb 11*c0500ff 84f920fe 40c02fe 60900fb 500ee 84f920fe 40c02fe 60c00fb 500ee
  //   437087b 1c37017e 6*c0500ff 84f920fe 40c02fe 60900fb 500ee 84f920fe 40c02fe 60c00fb 500ee 437087b
  //   1c37017e 6*c0500ff 84f920fe 40c02fe 60900fb 500ee 84f920fe 40c02fe 60c00fb 500ee 437087b 1c37017e
  //   6*c0500ff 84f920fe 40c02fe 60900fb 500ee 84f920fe 40c02fe 60c00fb 500ee 437087b 1c37017e 6*c0500ff
  //   84f920fe 4fc02fe 60900fb 500ee 84f920fe 4fc02fe 60c00fb 500ee 437087b 1c37017e 6*c0500ff 84f920fe
  //   4fc02fe 60900fb 500ee 84f920fe 4fc02fe 60c00fb 500ee 437087b 1c37017e 6*c0500ff 84f920fe 4fc02fe
  //   60900fb 500ee 84f920fe 4fc02fe 60c00fb 500ee 437087b 1c37017e 6*c0500ff 84f920fe 4fc02fe 60900fb
  //   500ee 84f920fe 4fc02fe 60c00fb 500ee 437087b 1c37017e 6*c0500ff a401087b 40401fb 4a7107b 840108fb
  //   c0401fb 11*c0500ff a401087b 40401fb 4a7107b 840108fb c0401fb 11*c0500ff a401087b 40401fb 4a7107b
  //   840108fb c0401fb 11*c0500ff a401087b 40401fb 4a7107b 840108fb c0401fb 11*c0500ff a401087b 40c01fb
  //   4a7107b 840108fb c0c01fb 11*c0500ff a401087b 40c01fb 4a7107b 840108fb c0c01fb 11*c0500ff a401087b
  //   40c01fb 4a7107b 840108fb c0c01fb 11*c0500ff a401087b 40c01fb 4a7107b 840108fb c0c01fb 11*c0500ff
  //   84f920fe 40c02fe 60900fb 500ee 84f920fe 40c02fe 60c00fb 500ee 437087b 1c37017e 6*c0500ff 84f920fe
  //   40c02fe 60900fb 500ee 84f920fe 40c02fe 60c00fb 500ee 437087b 1c37017e 6*c0500ff 84f920fe 40c02fe
  //   60900fb 500ee 84f920fe 40c02fe 60c00fb 500ee 437087b 1c37017e 6*c0500ff 84f920fe 40c02fe 60900fb
  //   500ee 84f920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
  //   EEROM A
  //   EEROM C
  //   Write on clock falling edge
  //   EEROM B
  //   EEROM D
endmodule
